# Fritzing sketch c16Weather (saved by Fritzing 0.7.10b)
breadboards: 1

parts:
  Arduino1 = Arduino
  R1 = Photocell (LDR) [package=THT]
  R2 = Resistor [tolerance=±5% resistance=220 package=THT]
  Part1 = Barometric Pressure Sensor - BMP085 Breakout
  RHT1 = Humidity and Temperature Sensor RHT03
  Q1 = NPN-Transistor [package="TO92 [THT]"]
  D1 = Rectifier Diode [part_number=1N4001 package="300 mil [THT]"]
  R3 = Resistor [tolerance=±5% resistance=220 package=THT]
  R4 = Resistor [tolerance=±5% resistance=220 package=THT]
  U1 = mystery part, 4 pins [chip_label=?]
  U2 = mystery part, 2 pins [chip_label=?]
  U3 = mystery part, 4 pins [chip_label=?]
  R5 = Resistor [tolerance=±5% resistance=220 package=THT]
  LED1 = LED - 5mm [color="Red (633nm)" package="5 mm [THT]"]
  R6 = Resistor [tolerance=±5% resistance=220 package=THT]

nets:
  N1: Arduino1.D2, R5.Pin_0, LED1.anode
  N2: Arduino1.A0, R3.Pin_0
  N3: Arduino1.A2, RHT1.Data-signal
  N4: Arduino1.A3, R1.pin_0, R2.Pin_1
  N5: Arduino1.A4, Part1.SCL, U1.pin3, U3.pin3
  N6: Arduino1.A5, Part1.SDA, U1.pin4, U3.pin4
  N7: R1.pin_1, Part1.GND, RHT1.GND_2, Q1.E, Q1.C, U1.pin2, U3.pin2, R5.Pin_1
  N8: R2.Pin_0, Part1.VCC, RHT1.GND_1, Q1.B, R4.Pin_0, U1.pin1, U2.pin2, U3.pin1, R6.Pin_0
  N9: D1.cathode, U2.pin1
  N10: D1.anode, R3.Pin_1, R4.Pin_1
  N11: LED1.cathode, R6.Pin_1

notes:
  Hall Effect Normaly Open, South Closed
  solar
  BMP085
  DHT22
  pinMode(2, INPUT);
  digitalWrite(2, HIGH);
  CDS
  RTC DS1307
  TSL2561
  Gotta have a blinky
